// Logisim project control-logic.circ as structural Verilog: 1 circuit, main circuit control_logic
module control_logic (
  input  [31:0] Instruction,
  input  BrEq,
  input  BrLt,
  output PCSel,
  output RegWEn,
  output [2:0] ImmSel,
  output BrUn,
  output ASel,
  output BSel,
  output [3:0] ALUSel,
  output MemWEn,
  output [1:0] WBSel
);

  wire and_1_out, and_2_out, and_3_out, comparator_1_eq, comparator_2_eq, comparator_3_eq, comparator_4_eq,
       comparator_5_eq, comparator_6_eq, comparator_7_eq, or_1_out, undriven_37, undriven_39, undriven_40,
       undriven_42, undriven_43, undriven_45, undriven_46, undriven_49, undriven_50, undriven_53,
       undriven_54, undriven_57, undriven_58, undriven_61, undriven_62, undriven_64, undriven_65,
       undriven_67, undriven_71, undriven_72, undriven_73, undriven_74, undriven_75, undriven_76,
       undriven_77, undriven_78, undriven_79;
  wire [1:0] undriven_44, undriven_47, undriven_51, undriven_55, undriven_59, undriven_63, undriven_66,
       undriven_68, undriven_69;
  wire [3:0] Branch_alu, format, funct3_edit, I_alu, I_funct7, J_alu, R_alu, R_funct7_0x0, R_funct7_0x01,
       R_funct7_0x05, S_alu, U_alu, undriven_19, undriven_20, undriven_21, undriven_22, undriven_23,
       undriven_24, undriven_25, undriven_26, undriven_27, undriven_28, undriven_29, undriven_30,
       undriven_31, undriven_32, undriven_33, undriven_34, undriven_35, undriven_36, undriven_38,
       undriven_41, undriven_48, undriven_52, undriven_56, undriven_60, undriven_70, undriven_80;
  wire [4:0] multiplexer_1_out, multiplexer_2_out, opcode2_6, undriven, undriven_2, undriven_3, undriven_4,
       undriven_5, undriven_6, undriven_7, undriven_8, undriven_9, undriven_10, undriven_11, undriven_12,
       undriven_13, undriven_14, undriven_15, undriven_16, undriven_17, undriven_18;
  wire [15:0] rom_1_data;

  Comparator #(.width(5)) comparator_1 (.a(opcode2_6), .b(5'b01000), .eq(comparator_1_eq));  // open: gt, lt
  Comparator #(.width(3)) comparator_2 (.a(Instruction[14:12]), .b(3'b010), .eq(comparator_2_eq));  // open: gt, lt
  ROM #(.addrWidth(6), .dataWidth(16)) rom_1 (.data(rom_1_data));  // open: addr
  Comparator #(.mode("unsigned"), .width(4)) comparator_3 (
    .a(format), .b(4'b0100), .eq(comparator_3_eq));  // open: gt, lt
  Comparator #(.mode("unsigned"), .width(4)) comparator_4 (
    .a(funct3_edit), .b(4'b0011), .eq(comparator_4_eq));  // open: gt, lt
  Comparator #(.mode("unsigned"), .width(4)) comparator_5 (
    .a(format), .b(4'b1000), .eq(comparator_5_eq));  // open: gt, lt
  Comparator #(.mode("unsigned"), .width(4)) comparator_6 (
    .a(funct3_edit), .b(4'b0110), .eq(comparator_6_eq));  // open: gt, lt
  Comparator #(.mode("unsigned"), .width(4)) comparator_7 (
    .a(funct3_edit), .b(4'b0111), .eq(comparator_7_eq));  // open: gt, lt
  Multiplexer #(.enable("false"), .select(4), .width(5)) multiplexer_1 (
    .in0(undriven), .in1(undriven_2), .in2(undriven_3), .in3(undriven_4), .in4(undriven_6), .in5(undriven_8),
    .in6(undriven_10), .in7(undriven_12), .in8(undriven_14), .out(multiplexer_1_out), .sel(format));  // open: in9, in10, in11, in12, in13, in14, in15
  // Probe on multiplexer_2_out
  Multiplexer #(.enable("false"), .select(4), .width(5)) multiplexer_2 (
    .in0(undriven_5), .in1(undriven_7), .in2(undriven_9), .in3(undriven_11), .in4(undriven_13),
    .in5(undriven_15), .in6(undriven_16), .in7(undriven_17), .in8(undriven_18), .out(multiplexer_2_out),
    .sel(format));  // open: in9, in10, in11, in12, in13, in14, in15
  or or_1 (or_1_out, comparator_6_eq, comparator_7_eq);
  // Probe on MemWEn
  Multiplexer #(.enable("false"), .select(4)) multiplexer_3 (
    .in0(1'b0), .in1(1'b0), .in2(1'b0), .in3(1'b0), .in4(1'b0), .in5(1'b0), .in6(1'b0), .in7(1'b0),
    .in8(and_1_out), .out(MemWEn), .sel(format));  // open: in9, in10, in11, in12, in13, in14, in15
  and and_1 (and_1_out, comparator_1_eq, comparator_2_eq);
  // Probe on multiplexer_1_out
  and and_2 (and_2_out, comparator_3_eq, comparator_4_eq);
  // Probe on ALUSel
  Multiplexer #(.enable("false"), .select(4), .width(4)) multiplexer_4 (
    .in0(I_alu), .in1(I_alu), .in2(U_alu), .in3(S_alu), .in4(R_alu), .in5(U_alu), .in6(J_alu), .in7(J_alu),
    .in8(Branch_alu), .out(ALUSel), .sel(format));  // open: in9, in10, in11, in12, in13, in14, in15
  and and_3 (and_3_out, comparator_5_eq, or_1_out);
  or or_2 (BrUn, and_2_out, and_3_out);
  Multiplexer #(.enable("false"), .select(5), .width(4)) multiplexer_5 (
    .in0(4'b0000), .in1(undriven_19), .in2(undriven_20), .in3(undriven_21), .in4(4'b0001), .in5(4'b0010),
    .in6(undriven_22), .in7(undriven_23), .in8(4'b0011), .in9(undriven_24), .in10(undriven_25),
    .in11(undriven_26), .in12(4'b0100), .in13(4'b0101), .in14(undriven_27), .in15(undriven_28),
    .in16(undriven_29), .in17(undriven_30), .in18(undriven_31), .in19(undriven_32), .in20(undriven_33),
    .in21(undriven_34), .in22(undriven_35), .in23(undriven_36), .in24(4'b1000), .in25(4'b0111),
    .in26(undriven_41), .in27(4'b0110), .in28(undriven_48), .in29(undriven_52), .in30(undriven_56),
    .in31(undriven_60), .out(format), .sel(Instruction[6:2]));
  Multiplexer #(.enable("false"), .select(2), .width(4)) multiplexer_6 (
    .in0(4'b0101), .in1(undriven_38), .in2(4'b1101), .out(I_funct7), .sel({Instruction[31], Instruction[25]}));  // open: in3
  // Probe on PCSel
  Multiplexer #(.enable("false"), .select(4)) multiplexer_7 (
    .in0(undriven_37), .in1(undriven_39), .in2(undriven_42), .in3(undriven_45), .in4(undriven_49),
    .in5(undriven_53), .in6(undriven_57), .in7(undriven_61), .in8(undriven_64), .out(PCSel), .sel(format));  // open: in9, in10, in11, in12, in13, in14, in15
  Multiplexer #(.enable("false"), .select(4)) multiplexer_8 (
    .in0(undriven_40), .in1(undriven_43), .in2(undriven_46), .in3(undriven_50), .in4(undriven_54),
    .in5(undriven_58), .in6(undriven_62), .in7(undriven_65), .in8(undriven_67), .out(ASel), .sel(format));  // open: in9, in10, in11, in12, in13, in14, in15
  Multiplexer #(.enable("false"), .select(4), .width(2)) multiplexer_9 (
    .in0(undriven_44), .in1(undriven_47), .in2(undriven_51), .in3(undriven_55), .in4(undriven_59),
    .in5(undriven_63), .in6(undriven_66), .in7(undriven_68), .in8(undriven_69), .out(WBSel), .sel(format));  // open: in9, in10, in11, in12, in13, in14, in15
  // Probe on I_alu
  Multiplexer #(.enable("false"), .select(4), .width(4)) multiplexer_10 (
    .in0(funct3_edit), .in1(funct3_edit), .in2(funct3_edit), .in3(funct3_edit), .in4(funct3_edit),
    .in5(I_funct7), .in6(funct3_edit), .in7(funct3_edit), .in8(funct3_edit), .out(I_alu), .sel(funct3_edit));  // open: in9, in10, in11, in12, in13, in14, in15
  assign funct3_edit = {{1{1'b0}}, Instruction[14:12]};  // Bit_Extender bit_extender_1
  // Probe on ASel
  // Probe on WBSel
  Multiplexer #(.enable("false"), .select(2), .width(4)) multiplexer_11 (
    .in0(4'b0000), .in1(4'b1000), .in2(4'b1100), .out(R_funct7_0x0), .sel({Instruction[31], Instruction[25]}));  // open: in3
  Multiplexer #(.enable("false"), .select(2), .width(4)) multiplexer_12 (
    .in0(4'b0101), .in1(undriven_70), .in2(4'b1101), .out(R_funct7_0x05),
    .sel({Instruction[31], Instruction[25]}));  // open: in3
  Multiplexer #(.enable("false"), .select(4)) multiplexer_13 (
    .in0(1'b1), .in1(1'b1), .in2(1'b1), .in3(1'b0), .in4(1'b1), .in5(1'b1), .in6(1'b1), .in7(1'b1),
    .in8(1'b0), .out(RegWEn), .sel(format));  // open: in9, in10, in11, in12, in13, in14, in15
  Multiplexer #(.enable("false"), .select(4)) multiplexer_14 (
    .in0(undriven_71), .in1(undriven_72), .in2(undriven_73), .in3(undriven_74), .in4(undriven_75),
    .in5(undriven_76), .in6(undriven_77), .in7(undriven_78), .in8(undriven_79), .out(BSel), .sel(format));  // open: in9, in10, in11, in12, in13, in14, in15
  // Probe on R_alu
  Multiplexer #(.enable("false"), .select(4), .width(4)) multiplexer_15 (
    .in0(R_funct7_0x0), .in1(R_funct7_0x01), .in2(funct3_edit), .in3(funct3_edit), .in4(funct3_edit),
    .in5(R_funct7_0x05), .in6(funct3_edit), .in7(funct3_edit), .in8(funct3_edit), .out(R_alu),
    .sel(funct3_edit));  // open: in9, in10, in11, in12, in13, in14, in15
  // Probe on RegWEn
  // Probe on BSel
  Multiplexer #(.enable("false"), .select(2), .width(4)) multiplexer_16 (
    .in0(4'b0001), .in1(4'b1001), .in2(undriven_80), .out(R_funct7_0x01),
    .sel({Instruction[31], Instruction[25]}));  // open: in3
  Multiplexer #(.enable("false"), .select(4), .width(3)) multiplexer_17 (
    .in0(3'b000), .in1(3'b000), .in2(3'b011), .in3(3'b001), .in4(3'b111), .in5(3'b011), .in6(3'b100),
    .in7(3'b100), .in8(3'b010), .out(ImmSel), .sel(format));  // open: in9, in10, in11, in12, in13, in14, in15
  // Probe on ImmSel

  // Other names for the same wires on the sheet: b_imm[12:1] = {Instruction[31], Instruction[7], Instruction[30:25], Instruction[11:8]};
  //   b_imm4_1[3:0] = Instruction[11:8]; b_imm10_5[5:0] = Instruction[30:25]; funct7[6:0] = Instruction[31:25];
  //   b_imm11 = Instruction[7]; funct3[2:0] = Instruction[14:12];
  //   funct7_edit[1:0] = {Instruction[31], Instruction[25]}; b_imm12 = Instruction[31];
  //   opcode_2_6[4:0] = Instruction[6:2]

  // Notes on the sheet:
  //   INPUTS to your circuit
  //   Connect ROM Input here ->
  //   Template
  //   Template
  //   Template
  //   ROM FOR CONTROL LOGIC
  //   Format Key:
  //   R-Format
  //   Branch-Format
  //   Format Key:
  //   S-Format = 3
  //   R-Format = 4
  //   Template
  //   Format Key:
  //   I-Format --> Load = 0
  //   U-Format auipc = 2
  //   S-Format = 3
  //   R-Format = 4
  //   U-Format lui = 5
  //   J-Format jal = 6
  //   J-Format jalr = 7
  //   Branch / Store = 8
  //   I-Format --> Load = 0
  //   I-Format --> imm log/arith = 1
  //   U-Format auipc = 2
  //   S-Format = 3
  //   R-Format = 4
  //   U-Format lui = 5
  //   J-Format jal = 6
  //   J-Format jalr = 7
  //   Branch / Store = 8
  //   I-Format --> Load = 0
  //   I-Format --> imm log/arith = 1
  //   U-Format auipc = 2
  //   U-Format lui = 5
  //   J-Format jal = 6
  //   J-Format jalr = 7
  //   Branch / Store = 8
  //   Format Key:
  //   U-Format auipc = 2
  //   S-Format = 3
  //   R-Format = 4
  //   U-Format lui = 5
  //   J-Format jal = 6
  //   J-Format jalr = 7
  //   Branch / Store = 8
  //   I-Format --> imm log/arith = 1
  //   DON'T CHANGE THE LOCATIONS OF THE INPUTS AND OUTPUTS!
  //   This is only if you choose to do the ROM option
  //   CONNECT
  //   WIRE
  //   TO
  //   USE
  //   ROM
  //   I-Format --> Load = 0
  //   I-Format --> imm log/arith = 1
  //   OUTPUT from your circuit
  //   Template
  //   Format Key:
  //   Format Key:
  //   Template
  //   Format Key:
  //   Format Key:
  //   Key:
  //   Reminder: If using ROM, use combinational logic for PCSel
  //   Format Key:
  //   S-Format = 3
  //   R-Format = 4
  //   U-Format lui = 5
  //   J-Format jal = 6
  //   J-Format jalr = 7
  //   Branch / Store = 8
  //   Opcode Key:
  //   R-Format = 12
  //   S-Format = 8
  //   I-Format --> Load = 0
  //   I-Format --> imm log/arith = 1
  //   U-Format auipc = 2
  //   S-Format = 3
  //   R-Format = 4
  //   U-Format lui = 5
  //   J-Format jal = 6
  //   J-Format jalr = 7
  //   Branch / Store = 8
  //   I-Format --> Load = 0
  //   I-Format --> imm log/arith = 1
  //   U-Format auipc = 2
  //   S-Format = 3
  //   R-Format = 4
  //   U-Format lui = 5
  //   J-Format jal = 6
  //   J-Format jalr = 7
  //   Branch / Store = 8
  //   I-Format --> Load = 0
  //   U-Format auipc = 2
  //   S-Format = 3
  //   R-Format = 4
  //   U-Format lui = 5
  //   J-Format jal = 6
  //   J-Format jalr = 7
  //   Branch / Store = 8
  //   I-Format --> Load = 0
  //   I-Format --> imm log/arith = 1
  //   U-Format auipc = 2
  //   S-Format = 3
  //   R-Format = 4
  //   U-Format lui = 5
  //   J-Format jal = 6
  //   J-Format jalr = 7
  //   Branch / Store = 8
  //   0 == 0 --> srl  = 5
  //   0b01 = 1 --> n/a
  //   0b10 = 2 --> sra = 13
  //   I-Format --> Load = 0
  //   I-Format --> imm log/arith = 1
  //   U-Format auipc = 2
  //   Branch / Store = 24
  //   J-Format --> jalr = 25; jal = 27
  //   U-Format --> auipc = 5; lui = 3
  //   I-Format --> imm log/arith = 1
  //   I-Format --> immediate log/arith = 4; load = 0
  //   Key:
  //   Key:
  //   0 --> add = 0
  //   1 = mul --> 8
  //   2 = sub --> 12
  //   0 --> srl = 5
  //   1 = n/a
  //   2 = sra --> 13
  //   Template
  //   Format Key:
  //   Template
  //   Format Key:
  //   Format Key:
  //   S-Format = 3
  //   R-Format = 4
  //   U-Format lui = 5
  //   J-Format jal = 6
  //   J-Format jalr = 7
  //   I-Format --> Load = 0
  //   U-Format auipc = 2
  //   S-Format = 3
  //   R-Format = 4
  //   U-Format lui = 5
  //   J-Format jal = 6
  //   J-Format jalr = 7
  //   Branch / Store = 8
  //   I-Format --> Load = 0
  //   U-Format auipc = 2
  //   S-Format = 3
  //   R-Format = 4
  //   U-Format lui = 5
  //   J-Format jal = 6
  //   J-Format jalr = 7
  //   Branch / Store = 8
  //   I-Format --> Load = 0
  //   I-Format --> imm log/arith = 1
  //   U-Format auipc = 2
  //   Branch / Store = 8
  //   Key:
  //   I-Format --> imm log/arith = 1
  //   I-Format --> imm log/arith = 1
  //   0 --> sll = 1
  //   1 = mulh -->9
  //   2 = n/a
  //   ALU Key:
  //   add = 0
  //   sll = 1
  //   slt = 2
  //   xor = 4
  //   srl = 5
  //   or = 6
  //   and = 7
  //   mul (sign) = 8
  //   mulh (sign) = 9
  //   mulhu = 11
  //   sub = 12
  //   sra = 13
  //   bsel = 15
  //   Template
  //   Format Key:
  //   I-Format --> Load = 0
  //   U-Format auipc = 2
  //   S-Format = 3
  //   R-Format = 4
  //   U-Format lui = 5
  //   J-Format jal = 6
  //   J-Format jalr = 7
  //   Branch / Store = 8
  //   I-Format --> imm log/arith = 1
endmodule
